# Fritzing sketch diseño protoboard (saved by Fritzing 0.9.1b)
breadboards: 1

parts:
  S1 = Pushbutton [package="[THT]"]
  S2 = Pushbutton [package="[THT]"]
  S3 = Pushbutton [package="[THT]"]
  S4 = Pushbutton [package="[THT]"]
  S5 = Pushbutton [part_number=start package="[THT]"]
  Launchpad1 = TI Launchpad MSP430G2
  LED1 = smd LED [color="Red (633nm)" package="1206 [SMD]"]
  U1 = POT [package=pot_alpha_rv16af-20]
  J1 = Piezo Speaker
  LED2 = smd LED [color="Yellow (595nm)" package="1206 [SMD]"]
  LED3 = smd LED [color="Green (565nm)" package="1206 [SMD]"]
  LED4 = smd LED [color="Blue (470nm)" package="1206 [SMD]"]
  R1 = Resistor [tolerance=±5% resistance=220 package=THT]
  R2 = Resistor [tolerance=±5% resistance=220 package=THT]
  R3 = Resistor [tolerance=±5% resistance=220 package=THT]
  R4 = Resistor [tolerance=±5% resistance=220 package=THT]

nets:
  N1: S1.Pin_1, S1.Pin_2, S2.Pin_1, S2.Pin_2, S3.Pin_1, S3.Pin_2, S4.Pin_1, S4.Pin_2, S5.Pin_1, S5.Pin_2, Launchpad1.p20, LED1.cathode, U1.A, J1.pin1, LED2.cathode, LED3.cathode, LED4.cathode
  N2: S1.Pin_3, S1.Pin_4, Launchpad1.p4
  N3: S2.Pin_3, S2.Pin_4, Launchpad1.p5
  N4: S3.Pin_3, S3.Pin_4, Launchpad1.p6
  N5: S4.Pin_3, S4.Pin_4, Launchpad1.p7
  N6: S5.Pin_3, S5.Pin_4, Launchpad1.p8
  N7: Launchpad1.p3, U1.S
  N8: Launchpad1.p1, U1.E
  N9: Launchpad1.p11, R2.Pin_0
  N10: Launchpad1.p12, R1.Pin_0
  N11: Launchpad1.p13, R3.Pin_0
  N12: Launchpad1.p14, R4.Pin_0
  N13: Launchpad1.p15, J1.pin2
  N14: LED1.anode, R4.Pin_1
  N15: LED2.anode, R3.Pin_1
  N16: LED3.anode, R1.Pin_1
  N17: LED4.anode, R2.Pin_1
